// Logisim project Computer Architecture 8-Bit CPU Design Project.circ as structural Verilog: 4 circuits, main circuit ALU
module main (
  input  [7:0] in_1,
  input  in_2,
  input  START,
  output [7:0] out_4,
  output [7:0] IR
);

  wire alu_1_c_flag, alu_1_n_flag, alu_1_v_flag, alu_1_z_flag, ALU_OP, Clk, d_ff_1_q, En_IR, En_MAR, En_MBR,
       En_PC_Inc, En_RgA, En_RgA_OP, En_RgB, En_RgB_OP, En_RgC, En_RgC_OP, En_RgD, En_RgD_OP, En_TempReg1,
       En_TempReg2, HALT_SIG, Ld_PC, Masked_Bit, MBR_OP, or_1_out, or_2_out, PC_OP, RAM_OP, Step_Reset,
       Write_RAM;
  wire [2:0] counter_1_q;
  wire [7:0] alu_1_alu_result, controlled_buffer_2_out, register_1_q, register_2_q,
       system_registers_1_mar_out, system_registers_1_mbr_out, system_registers_1_pc_out;
  wire [23:23] rom_1_data;

  Register_File register_file_1 (
    .Clk(Clk), .Reg_Data_In(in_1), .En_RgA(En_RgA), .En_RgB(En_RgB), .En_RgC(En_RgC), .En_RgD(En_RgD),
    .Clr_Reg(in_2), .Reg_Data_Out(in_1), .RegA_OUT(En_RgA_OP), .RegB_OUT(En_RgB_OP), .RegC_OUT(En_RgC_OP),
    .RegD_OUT(En_RgD_OP));
  Register register_1 (.D(in_1), .en(En_TempReg1), .Q(register_1_q), .clk(Clk), .clr(in_2));
  Register register_2 (.D(in_1), .en(En_TempReg2), .Q(register_2_q), .clk(Clk), .clr(in_2));
  ALU alu_1 (
    .INPUT_A(register_1_q), .INPUT_B(register_2_q), .Opcode(IR[7:4]), .V_Flag(alu_1_v_flag),
    .C_Flag(alu_1_c_flag), .N_Flag(alu_1_n_flag), .ALU_RESULT(alu_1_alu_result), .Z_Flag(alu_1_z_flag));
  LED Overflow (.in(alu_1_v_flag));
  LED Carry (.in(alu_1_c_flag));
  LED Negative (.in(alu_1_n_flag));
  LED Zero__A_B (.in(alu_1_z_flag));
  assign in_1 = ALU_OP ? alu_1_alu_result : 8'bz;  // Controlled_Buffer controlled_buffer_1
  D_Flip_Flop d_ff_1 (.clk(START), .D(1'b1), .Q(d_ff_1_q), .reset(or_1_out));  // open: Qn, preset, en
  or or_1 (or_1_out, HALT_SIG, in_2);
  Clock clock_1 (.out(Clk));
  Counter #(.width(3), .max('h7)) counter_1 (
    .count(d_ff_1_q), .Q(counter_1_q), .clk(Clk), .clr(or_2_out));  // open: load, D, carry
  or or_2 (or_2_out, in_2, Step_Reset);
  System_Registers system_registers_1 (
    .Data_Bus_In(in_1), .PC_Out(system_registers_1_pc_out), .MAR_Out(system_registers_1_mar_out),
    .MBR_Out(system_registers_1_mbr_out), .IR_Out(IR), .Reset(in_2), .load(Ld_PC), .Clk(Clk),
    .en_PC(En_PC_Inc), .en_MAR(En_MAR), .en_MBR(En_MBR), .en_PC_2(En_IR),
    .Memory_Bus_In(controlled_buffer_2_out));
  assign controlled_buffer_2_out = Masked_Bit ? {4'b1111, IR[3:0]} : 8'bz;  // Controlled_Buffer controlled_buffer_2
  assign controlled_buffer_2_out = PC_OP ? system_registers_1_pc_out : 8'bz;  // Controlled_Buffer controlled_buffer_3
  assign in_1 = MBR_OP ? system_registers_1_mbr_out : 8'bz;  // Controlled_Buffer controlled_buffer_4
  ROM #(.addrWidth(7), .dataWidth(24)) rom_1 (
    .addr({IR[7:4], counter_1_q}),
    .data({rom_1_data[23], HALT_SIG, Write_RAM, Step_Reset, En_RgD_OP, En_RgC_OP, En_RgB_OP, En_RgA_OP, En_RgD, En_RgC, En_RgB, En_RgA, En_TempReg2, En_TempReg1, En_PC_Inc, Ld_PC, En_IR, En_MBR, En_MAR, Masked_Bit, ALU_OP, MBR_OP, RAM_OP, PC_OP}),
    .sel(1'b1));
  RAM ram_1 (.addr(system_registers_1_mar_out), .data(in_1), .sel(RAM_OP), .clk(Clk), .ld(Write_RAM), .clr(in_2));

  assign out_4 = in_1;

  // Other names for the same wires on the sheet: OPCODE[3:0] = IR[7:4]; Reset = in_2

  // Notes on the sheet:
  //   contents of rom_1 (hex, n*v repeats v):
  //   200021 200242 200084 220800 210400 201008 300000 0 200021 200242 200084 220800 210400 201008 300000
  //   0 200021 200242 200084 220800 210400 201008 300000 0 200021 200242 200084 20800 210400 201008 300000
  //   0 200021 200242 200084 210400 201008 300000 0 0 200021 200242 200084 210400 201008 300000 0 0 200021
  //   200242 200084 210400 201008 300000 0 0 200021 200242 200084 210400 201008 300000 0 0 200021 200242
  //   200084 210400 201008 300000 0 0 200021 200242 200084 212000 300000 0 0 0 200021 200242 200084 200030
  //   201002 300000 0 0 200021 200242 200084 200110 300000 0 0 0 200021 200242 200084 200030 10002 300000
  //   0 0 200021 200242 200084 214000 300000 0 0 0 200021 200242 200084 218000 300000 0 0 0 200021 200242
  //   200084 400000
endmodule

module ALU (
  input  [7:0] INPUT_A,
  input  [7:0] INPUT_B,
  input  [3:0] Opcode,
  output V_Flag,
  output C_Flag,
  output N_Flag,
  output [7:0] ALU_RESULT,
  output Z_Flag
);

  wire adder_1_cout, adder_2_cout, subtractor_1_bout, subtractor_2_bout, xnor_1_out, xor_1_out;
  wire [7:0] adder_1_out, adder_2_out, and_1_out, not_1_out, or_1_out, shifter_1_out, shifter_2_out,
       subtractor_1_out, subtractor_2_out;

  Adder adder_1 (.a(INPUT_A), .b(INPUT_B), .out(adder_1_out), .cin(1'b0), .cout(adder_1_cout));
  Subtractor subtractor_1 (.a(INPUT_A), .b(INPUT_B), .out(subtractor_1_out), .bin(1'b0), .bout(subtractor_1_bout));
  assign and_1_out = INPUT_A & INPUT_B;  // AND_Gate and_1, 8 bits wide
  assign or_1_out = INPUT_A | INPUT_B;  // OR_Gate or_1, 8 bits wide
  assign not_1_out = ~INPUT_A;  // NOT_Gate not_1, 8 bits wide
  Shifter shifter_1 (.in(INPUT_A), .\dist (3'b001), .out(shifter_1_out));
  Shifter #(.shift("lr")) shifter_2 (.in(INPUT_A), .\dist (3'b001), .out(shifter_2_out));
  Adder adder_2 (.a(INPUT_A), .b(8'h1), .out(adder_2_out), .cin(1'b0), .cout(adder_2_cout));
  Subtractor subtractor_2 (.a(INPUT_A), .b(8'h1), .out(subtractor_2_out), .bin(1'b0), .bout(subtractor_2_bout));
  Multiplexer #(.select(4), .width(8), .enable("false")) multiplexer_1 (
    .in0(adder_1_out), .in1(subtractor_1_out), .in2(and_1_out), .in3(or_1_out), .in4(not_1_out),
    .in5(shifter_1_out), .in6(shifter_2_out), .in7(adder_2_out), .in8(subtractor_2_out), .in9(INPUT_A),
    .in10(INPUT_B), .in11(INPUT_A), .in12(INPUT_A), .in13(INPUT_B), .in14({8{1'b0}}), .in15({8{1'b0}}),
    .out(ALU_RESULT), .sel(Opcode));
  Comparator comparator_1 (.a(ALU_RESULT), .b({8{1'b0}}), .eq(Z_Flag));  // open: gt, lt
  xnor xnor_1 (xnor_1_out, INPUT_B[7], INPUT_A[7]);
  xor xor_1 (xor_1_out, INPUT_A[7], adder_1_out[7]);
  and and_2 (V_Flag, xnor_1_out, xor_1_out);
  Multiplexer #(.select(4), .enable("false")) multiplexer_2 (
    .in0(adder_1_cout), .in1(1'b0), .in2(subtractor_1_bout), .in3(1'b0), .in4(1'b0), .in5(1'b0), .in6(1'b0),
    .in7(adder_2_cout), .in8(subtractor_2_bout), .in9(1'b0), .in10(1'b0), .in11(1'b0), .in12(1'b0),
    .in13(1'b0), .in14(1'b0), .in15(1'b0), .out(C_Flag), .sel(Opcode));

  assign N_Flag = ALU_RESULT[7];
endmodule

module Register_File (
  input  Clk,
  input  [7:0] Reg_Data_In,
  input  En_RgA,
  input  RegA_OUT,
  input  En_RgB,
  input  RegB_OUT,
  input  En_RgC,
  input  RegC_OUT,
  input  En_RgD,
  input  RegD_OUT,
  input  Clr_Reg,
  output [7:0] Reg_Data_Out
);

  wire [7:0] A_q, B_q, C_q, D_q;

  Register A (.D(Reg_Data_In), .en(En_RgA), .Q(A_q), .clk(Clk), .clr(Clr_Reg));
  Register B (.D(Reg_Data_In), .en(En_RgB), .Q(B_q), .clk(Clk), .clr(Clr_Reg));
  Register C (.D(Reg_Data_In), .en(En_RgC), .Q(C_q), .clk(Clk), .clr(Clr_Reg));
  Register D (.D(Reg_Data_In), .en(En_RgD), .Q(D_q), .clk(Clk), .clr(Clr_Reg));
  assign Reg_Data_Out = RegA_OUT ? A_q : 8'bz;  // Controlled_Buffer controlled_buffer_1
  assign Reg_Data_Out = RegB_OUT ? B_q : 8'bz;  // Controlled_Buffer controlled_buffer_2
  assign Reg_Data_Out = RegC_OUT ? C_q : 8'bz;  // Controlled_Buffer controlled_buffer_3
  assign Reg_Data_Out = RegD_OUT ? D_q : 8'bz;  // Controlled_Buffer controlled_buffer_4

  // Notes on the sheet:
  //   Register File
endmodule

module System_Registers (
  input  load,
  input  en_PC,
  input  [7:0] Memory_Bus_In,
  input  en_MAR,
  input  [7:0] Data_Bus_In,
  input  en_MBR,
  input  en_PC_2,
  input  Clk,
  input  Reset,
  output [7:0] PC_Out,
  output [7:0] MAR_Out,
  output [7:0] MBR_Out,
  output [7:0] IR_Out
);

  Counter counter_1 (.load(load), .D(Data_Bus_In), .count(en_PC), .Q(PC_Out), .clk(Clk), .clr(Reset));  // open: carry
  Register Memory_Address_Register (.D(Memory_Bus_In), .en(en_MAR), .Q(MAR_Out), .clk(Clk), .clr(Reset));
  Register Memory_Buffer_Register (.D(Data_Bus_In), .en(en_MBR), .Q(MBR_Out), .clk(Clk), .clr(Reset));
  Register Instruction_Register (.D(Data_Bus_In), .en(en_PC_2), .Q(IR_Out), .clk(Clk), .clr(Reset));
endmodule
